# Fritzing sketch activity1 (saved by Fritzing 0.9.1b)
breadboards: 1

parts:
  LED1 = smd LED [color="Red (635nm)" package="1206 [SMD]"]
  Raspberry_Pi1 = Raspberry Pi B+

nets:
  N1: LED1.cathode, Raspberry_Pi1.GND
  N2: LED1.anode, Raspberry_Pi1.GPIO4
