# Fritzing sketch activity2 (saved by Fritzing 0.9.1b)
breadboards: 1

parts:
  Raspberry_Pi1 = Raspberry Pi B+
  J1 = Piezo Speaker

nets:
  N1: Raspberry_Pi1.GPIO17, J1.pin2
  N2: Raspberry_Pi1.GND, J1.pin1
